# Fritzing sketch Schematic (saved by Fritzing 0.9.3b)
breadboards: 2

parts:
  Part1 = Arduino Uno (Rev3) - ICSP
  R1 = Slide Potentiometer [maximum_resistance=100kΩ]  # not connected
  R2 = Slide Potentiometer [maximum_resistance=100kΩ]  # not connected
  R3 = Slide Potentiometer [maximum_resistance=100kΩ]  # not connected
  R4 = Slide Potentiometer [maximum_resistance=100kΩ]  # not connected
  U1 = SWITCH_SPDT [package=kps-1290]
  U2 = SWITCH_SPDT [package=kps-1290]
  U3 = SWITCH_SPDT [package=kps-1290]
  U4 = SWITCH_SPDT [package=kps-1290]
  LED1 = LED - 3mm [color="Red (633nm)" package="3 mm [THT]"]
  LED2 = LED - 3mm [color="Red (633nm)" package="3 mm [THT]"]
  LED3 = LED - 3mm [color="Red (633nm)" package="3 mm [THT]"]
  LED4 = LED - 3mm [color="Red (633nm)" package="3 mm [THT]"]
  J1 = Dagu DGServo 9g header connector (female) [package=THT]
  J2 = Dagu DGServo 9g header connector (female) [package=THT]
  J3 = Dagu DGServo 9g header connector (female) [package=THT]
  J4 = Dagu DGServo 9g header connector (female) [package=THT]
  R13 = Resistor [tolerance=±5% resistance=220 package=THT]
  R14 = Resistor [tolerance=±5% resistance=220 package=THT]
  R15 = Resistor [tolerance=±5% resistance=220 package=THT]
  R16 = Resistor [tolerance=±5% resistance=220 package=THT]
  R17 = Resistor [tolerance=±5% resistance=220 package=THT]
  R18 = Resistor [tolerance=±5% resistance=220 package=THT]
  R19 = Resistor [tolerance=±5% resistance=220 package=THT]
  R20 = Resistor [tolerance=±5% resistance=220 package=THT]

nets:
  N1: Part1.GND, J1.pulse, J2.pulse, J3.pulse, J4.pulse, R13.Pin_1, R14.Pin_1, R15.Pin_1, R16.Pin_1, R17.Pin_1, R18.Pin_1, R19.Pin_1, R20.Pin_1
  N2: Part1.D9_PWM, J2.Vcc
  N3: Part1.D10_PWM/SS, J3.Vcc
  N4: Part1.D11_PWM/MOSI, J4.Vcc
  N5: Part1.D6_PWM, J1.Vcc
  N6: U1.O, R17.Pin_0
  GND: U1.P, U2.P, U3.P, U4.P, J1.gnd, J2.gnd, J3.gnd, J4.gnd
  N7: U2.O, R18.Pin_0
  N8: U3.O, R19.Pin_0
  N9: U4.O, R20.Pin_0
  N10: LED1.cathode, R13.Pin_0
  N11: LED2.cathode, R14.Pin_0
  N12: LED3.cathode, R15.Pin_0
  N13: LED4.cathode, R16.Pin_0
